# Fritzing sketch circuit_diagram_client_v1 (saved by Fritzing 0.9.3b)

parts:
  Part1 = Arduino Uno (Rev3)
  Part2 = Adafruit RFM9x LoRa Radio [part_number="Adafruit #3072 and #3073"]
  Nokia_5110_LCD_Module1 = Nokia_5110_LCD
  LED1 = LED - 5mm [color="Red (633nm)" package="5 mm [THT]"]

nets:
  N1: Part1.D8, Nokia_5110_LCD_Module1.connector6
  N2: Part1.D9_PWM, Part2.RST
  N3: Part1.D10_PWM/SS, Part2.CS
  N4: Part1.D11_PWM/MOSI, Part2.MOSI
  N5: Part1.D12/MISO, Part2.MISO
  N6: Part1.D13/SCK, Part2.SCK
  N7: Part1.D2, Part2.DIO0
  N8: Part1.D3_PWM, Nokia_5110_LCD_Module1.connector2
  N9: Part1.D4, Nokia_5110_LCD_Module1.connector3
  N10: Part1.D5_PWM, Nokia_5110_LCD_Module1.connector4
  N11: Part1.D6_PWM, LED1.cathode
  N12: Part1.D7, Nokia_5110_LCD_Module1.connector5
  N13: Part1.3V3, Nokia_5110_LCD_Module1.connector0, Nokia_5110_LCD_Module1.connector7
  5V: Part1.5V, Part2.VIN
  GND: Part1.GND, Part2.GND, Nokia_5110_LCD_Module1.connector1, LED1.anode

notes:
  Adafruit RFM69HCW Transceiver 868 or 915 MHz: https://www.adafruit.com/product/3070
  Nokia 5110 LCD

custom parts:
  Adafruit RFM9x LoRa Radio: Sending data over long distances is like magic, and now you can be a magician with this range of powerful and easy-to-use radio modules. Sure, sometimes you want to talk to a computer (a good time to use WiFi) or perhaps communicate with a Phone (choose Bluetooth Low Energy!) but what if you want to send data very far? Most WiFi, Bluetooth, Zigbee and other wireless chipsets use 2.4GHz, which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
